# Fritzing sketch Diagrama Solar Tracker (saved by Fritzing 1.0.0rc)
circuit board: 16.9333cm x 5.64444cm
breadboards: 1

parts:
  R1 = Resistor [tolerance=±5% resistance=51 power=0.25W package=THT]
  R2 = Resistor [tolerance=±5% resistance=100 power=0.25W package=THT]
  C1 = Electrolytic Capacitor [capacitance=1µF voltage=35V package="100 mil [THT, electrolytic]"]
  LED_PIN_12_(Left) = LED - 5mm [color="Blue (505nm)" current=0.030A package="5 mm [THT]"]
  LED_PIN_11_(Right) = LED - 5mm [color="Blue (505nm)" current=0.030A package="5 mm [THT]"]
  LED_PIN_13_(Down) = LED - 5mm [color="Red (633nm)" current=0.030A package="5 mm [THT]"]
  LED_PIN_10_(UP) = LED - 5mm [color="Blue (525nm)" current=0.030A part_number=Led_BTN_Automatico package="5 mm [THT]"]
  R9 = Resistor [tolerance=±5% resistance=220 power=0.25W package=THT]
  R10 = Resistor [tolerance=±5% resistance=220 power=0.25W package=THT]
  R11 = Resistor [tolerance=±5% resistance=220 power=0.25W package=THT]
  R12 = Resistor [tolerance=±5% resistance=220 power=0.25W package=THT]
  R5 = Resistor [tolerance=±5% resistance=220 power=0.25W package=THT]
  R4 = Resistor [tolerance=±5% resistance=220 power=0.25W package=THT]
  R3 = Resistor [tolerance=±5% resistance=220 power=0.25W package=THT]
  R6 = Resistor [tolerance=±5% resistance=220 power=0.25W package=THT]
  Servo_Vertical = Basic Servo [part_number="HiTec HS-422"]
  Foto_Celda = Solar Pannel [part_number=FotoSelda]
  LDR_2_Right_PIN_A1 = Photocell (LDR) [power=0.25W dark_resistance_@0.01lx=300kΩ light_resistance_@100lx=400Ω luminance=10lx package=THT]
  LDR_4_UP_PIN_A3 = Photocell (LDR) [power=0.25W dark_resistance_@0.01lx=300kΩ light_resistance_@100lx=400Ω luminance=10lx package=THT]
  LDR_3_Down_PIN_A2 = Photocell (LDR) [power=0.25W dark_resistance_@0.01lx=300kΩ light_resistance_@100lx=400Ω luminance=10lx package=THT]  # not connected
  LDR_1_Left_PIN_A0 = Photocell (LDR) [power=0.25W dark_resistance_@0.01lx=300kΩ light_resistance_@100lx=400Ω luminance=10lx package=THT]
  R8 = Rotary Potentiometer (Small) [maximum_resistance=10kΩ knob_status=50% power=0.5W package=THT]
  Tiny_RTC1 = Tiny RTC
  Componente1 = ACS712 Current Sensor 5A 20A 30A
  U2 = NodeMCU V3.0  # not connected
  Pla_Cprincipal = Arduino Mega 2560 (Rev3)
  Servo_Horizonal = Basic Servo [part_number="HiTec HS-422"]
  SD_card_module1 = SD Card Module
  OLED_I2C1 = OLED 128x64 I2C Monochrome Display

nets (from the breadboard view):
  GND: R1.Pin_0, C1.-, LED_PIN_12_(Left).cathode, LED_PIN_11_(Right).cathode, LED_PIN_13_(Down).cathode, LED_PIN_10_(UP).cathode, Servo_Vertical.gnd, R8.leg1, Componente1.GND, Pla_Cprincipal.A0, Pla_Cprincipal.A1, Pla_Cprincipal.A2, Pla_Cprincipal.A3, Servo_Horizonal.gnd, SD_card_module1.GND, SD_card_module1.+5
  N1: R2.Pin_1, Servo_Vertical.vcc, Foto_Celda.pin2
  N2: LED_PIN_12_(Left).anode, R11.Pin_1, Pla_Cprincipal.D12_PWM
  N3: LED_PIN_11_(Right).anode, R10.Pin_1, Pla_Cprincipal.D11_PWM
  N4: LED_PIN_13_(Down).anode, R12.Pin_1, Pla_Cprincipal.D13_PWM
  N5: LED_PIN_10_(UP).anode, R9.Pin_1, Pla_Cprincipal.D10_PWM
  N6: R5.Pin_0, LDR_2_Right_PIN_A1.pin_0
  N7: R5.Pin_1, R4.Pin_1, R3.Pin_1, R6.Pin_0, R8.leg2, Componente1.VCC
  N8: R3.Pin_0, LDR_4_UP_PIN_A3.pin_0
  N9: R6.Pin_1, LDR_1_Left_PIN_A0.pin_0
  N10: Foto_Celda.pin1, LDR_2_Right_PIN_A1.pin_1, LDR_4_UP_PIN_A3.pin_1, LDR_1_Left_PIN_A0.pin_1
  N11: Tiny_RTC1.SCL, Pla_Cprincipal.D21/SCL, OLED_I2C1.SCK
  N12: Tiny_RTC1.SDA, Pla_Cprincipal.D20/SDA, OLED_I2C1.SDA
  VCC: Tiny_RTC1.VCC, Pla_Cprincipal.5V, OLED_I2C1.VDD
  GND_2: Tiny_RTC1.GND, Pla_Cprincipal.GND, OLED_I2C1.GND
  N13: Componente1.OUT, Pla_Cprincipal.A4
  N14: Pla_Cprincipal.D50, SD_card_module1.MISO
  N15: Pla_Cprincipal.D51, SD_card_module1.MOSI
  N16: Pla_Cprincipal.D52, SD_card_module1.SCK
  N17: Pla_Cprincipal.D53, SD_card_module1.CS

custom parts:
  Tiny RTC: Tiny RTC I2C module DS1370Z RTC and AT24C32 EEPROM
  ACS712 Current Sensor 5A 20A 30A: Remix by Michael Kubina http://www.kubina.info Original by: https://forum.fritzing.org/t/current-sensor-5a-acs712/7694 https://forum.fritzing.org/u/ArtHome ArtHome12@gmail.com
  NodeMCU V3.0: ESP8266 based NodeMCU
  SD Card Module: SD Card Module Slot Socket Reader For Arduino ARM MCU
